# Fritzing sketch Y_EverSee (saved by Fritzing 0.9.3b)
circuit board: 8.46667cm x 5.64444cm

parts:
  元件1 = Arduino Nano (Rev3.0)
  元件2 = SRF05 Ultrasonic Rangefinder
  元件3 = Breakout Board for Electret Microphone

nets:
  GND: 元件1.GND, 元件2.GND, 元件3.AUD
  N1: 元件1.D2, 元件3.GND
  VCC: 元件1.5V, 元件2.VCC, 元件3.VCC
  N2: 元件1.A2, 元件2.Echo
  N3: 元件1.A1, 元件2.Trig
